# Fritzing sketch Ultrasound (saved by Fritzing 0.9.3b)
breadboards: 1

parts:
  J1 = Basic Servo
  부품1 = Arduino Uno (Rev3)
  hc-sr1 = hc-sr04

nets:
  GND: J1.gnd, 부품1.GND, hc-sr1.GND
  VCC: J1.vcc, 부품1.5V
  N1: J1.pulse, 부품1.D2
  N2: 부품1.D6_PWM, hc-sr1.Echo
  N3: 부품1.D7, hc-sr1.Trig
